// Digital circuit Lab00b.dig as structural Verilog
module Lab00b (
);

  wire led1_p1, switch2_b;

  Switch #(.switchActsAsInput("true")) switch2 (.A(1'b1), .B(switch2_b));
  // PolarityAwareLED led1: pin names not known; wires that end beside it: led1_p1, 1'b0
  Switch #(.switchActsAsInput("true")) switch1 (.A(switch2_b), .B(led1_p1));
endmodule
